# Fritzing sketch Snowtank (saved by Fritzing 0.9.3b)
breadboards: 4

parts:
  R1 = Resistor [tolerance=±5% resistance=770 package=THT]
  R2 = Resistor [tolerance=±5% resistance=770 package=THT]
  R3 = Resistor [tolerance=±5% resistance=1k package=THT]
  R7 = Resistor [tolerance=±5% resistance=220 package=THT]
  R8 = Resistor [tolerance=±5% resistance=1k package=THT]
  R9 = Resistor [tolerance=±5% resistance=1k package=THT]
  R10 = Resistor [tolerance=±5% resistance=1k package=THT]
  S1 = Pushbutton [package="[THT]"]
  S2 = Pushbutton [package="[THT]"]
  S3 = Pushbutton [package="[THT]"]
  S4 = Pushbutton [package="[THT]"]
  LED1 = LED - 5mm [color="Red (633nm)" package="5 mm [THT]"]
  LED2 = LED - 5mm [color="Red (633nm)" package="5 mm [THT]"]
  LED3 = LED - 5mm [color="White (4500K)" package="5 mm [THT]"]
  LED4 = LED - 5mm [color="White (4500K)" package="5 mm [THT]"]
  LED5 = LED - 5mm [color="Orange (620nm)" package="5 mm [THT]"]
  M1 = DC Motor
  M2 = DC Motor
  IC1 = L293D [package=THT]
  R11 = Resistor [tolerance=±5% resistance=220 package=THT]
  R12 = Resistor [tolerance=±5% resistance=220 package=THT]
  5V_VCC = 4 x AAA Battery Mount
  Q1 = NPN-Transistor [package="TO92 [THT]"]
  Q2 = NPN-Transistor [package="TO92 [THT]"]
  Part1 = Arduino Uno (Rev3)

nets (from the schematic view):
  N1: R1.Pin_0, Part1.D0/RX
  N2: R1.Pin_1, Q2.B
  N3: R2.Pin_0, Part1.D1/TX
  N4: R2.Pin_1, Q1.B
  N5: R3.Pin_0, S4.Pin_1, S4.Pin_2, Part1.D2
  N6: R3.Pin_1, R8.Pin_1, R9.Pin_1, R10.Pin_1, LED5.cathode, Q1.E, Q2.E, Part1.GND
  N7: R7.Pin_0, S1.Pin_3, S1.Pin_4, S2.Pin_3, S2.Pin_4, S3.Pin_3, S3.Pin_4, S4.Pin_3, S4.Pin_4, R11.Pin_0, R12.Pin_1, Part1.5V
  N8: R7.Pin_1, LED5.anode
  N9: R8.Pin_0, S3.Pin_1, S3.Pin_2, Part1.D3_PWM
  N10: R9.Pin_0, S2.Pin_1, S2.Pin_2, Part1.D4
  N11: R10.Pin_0, S1.Pin_1, S1.Pin_2, Part1.D5_PWM
  N12: LED1.cathode, LED2.cathode, Q2.C
  N13: LED1.anode, LED2.anode, R11.Pin_1
  N14: LED3.cathode, LED4.cathode, Q1.C
  N15: LED3.anode, LED4.anode, R12.Pin_0
  N16: M1.pin_1, IC1.Out_3_(_Controlled_by_Enable_2_)
  N17: M1.pin_2, IC1.Out_4_(_Controlled_by_Enable_2_)
  N18: M2.pin_1, IC1.Out_1_(_Controlled_by_Enable_1_)
  N19: M2.pin_2, IC1.Out_2_(_Controlled_by_Enable_1_)
  N20: IC1.Enable_1, Part1.D6_PWM
  N21: IC1.In_1, Part1.D7
  N22: IC1.0V, 5V_VCC.-
  N23: IC1.In_2, Part1.D8
  N24: IC1.+Vmotor, IC1.+V, 5V_VCC.+
  N25: IC1.Enable_2, Part1.D9_PWM
  N26: IC1.In_3, Part1.D10_PWM/SS
  N27: IC1.In_4, Part1.D11_PWM/MOSI

notes:
  Snow Tank Schematic
  by Kevin Yang

// code stored in the sketch: Snowtank code.ino
#define Right 2 // Button
#define Left 3 // Button
#define Forward 4 // Button
#define Backward 5 // Button
// Right motor
#define ENABLE1 6 
#define DIRA1 7
#define DIRB1 8
//Left Motor
#define ENABLE2 6
#define DIRA2 7
#define DIRB2 8

#define F_Leds 10 //Front Leds, controlled with a transiter
#define B_Leds 11 // back Leds, controlled with a transiter
void setup() {
for(int i = 0; i<6; i++){
digitalWrite(F_Leds, HIGH);
digitalWrite(B_Leds, HIGH);
delay(500);
digitalWrite(F_Leds, LOW);
digitalWrite(B_Leds, LOW);
delay(500);
}
pinMode(F_Leds,OUTPUT);
pinMode(B_Leds,OUTPUT);
pinMode(ENABLE1,OUTPUT);
pinMode(DIRA1,OUTPUT);
pinMode(DIRB1,OUTPUT);
pinMode(ENABLE2,OUTPUT);
pinMode(DIRA2,OUTPUT);
pinMode(DIRB2,OUTPUT);
pinMode(Right, INPUT);
pinMode(Left, INPUT);
pinMode(Forward, INPUT);
pinMode(Backward, INPUT);
}

void loop() {
  digitalRead(Left);
  digitalRead(Right);
  digitalRead(Forward);
  digitalRead(Backward);
  delay(5);
while (Left == HIGH){
  digitalWrite(DIRA1,LOW);
  digitalWrite(DIRB1,HIGH);
  digitalWrite(DIRA2,HIGH); 
  digitalWrite(DIRB2,LOW);
  delay(5);
}
while (Right == HIGH){
  digitalWrite(DIRA1,HIGH);
  digitalWrite(DIRB1,LOW);
  digitalWrite(DIRA2,LOW); 
  digitalWrite(DIRB2,HIGH);
  delay(5);
}
while (Forward == HIGH){
  digitalWrite(DIRA1,HIGH);
  digitalWrite(DIRB1,LOW);
  digitalWrite(DIRA2,HIGH); 
  digitalWrite(DIRB2,LOW);
  delay(5);
}
while (Backward == HIGH){
  digitalWrite(DIRA1,LOW);
  digitalWrite(DIRB1,HIGH);
  digitalWrite(DIRA2,LOW); 
  digitalWrite(DIRB2,HIGH);
  delay(5);
}

}
